# Fritzing sketch joy stick (saved by Fritzing 0.9.4)

parts:
  Part1 = Arduino Uno (Rev3)
  Part2 = Thumb Joystick
  R1 = Textile Potentiometer [part_number=PW064]  # not connected

nets:
  N1: Part1.A1, Part2.VERT
  N2: Part1.D2, Part2.VCC
  N3: Part1.5V, Part2.SEL
  GND: Part1.GND, Part2.GND
